// Logisim project processador_vilw.circ as structural Verilog: 12 circuits, main circuit main
module main (
);

  wire clk, is_move, is_zero, MemRead, MemWrite, moveh_l, MuxL1Src, RegWriteL1, RegWriteL3, RegWriteL4,
       reset, Sig_BNZR, Sig_BRZI, Sig_BRZR, Sig_JR;
  wire [1:0] multiplexer_2_out, pc_control_1_muxpc, RaLn3, RaLn4, RbLn3, RbLn4;
  wire [2:0] control_1_opula1, control_1_opula2;
  wire [3:0] restol1, restol2;
  wire [7:0] adder_1_out, adder_2_out, addr, bit_extender_2_out, breg_1_oaln2, breg_1_oaln3, breg_1_oaln4,
       breg_1_obln2, breg_1_obln3, breg_1_obln4, DadoL3, DadoL4, dadomem, dadosmem, move_1_movh, move_1_movl,
       multiplexer_1_out, multiplexer_3_out, multiplexer_4_out, register_1_q;
  wire [31:0] bit_extender_1_out;
  wire [31:4] dualram_1_p9;

  Clock clock_1 (.out(clk));
  Register register_1 (.D(multiplexer_1_out), .en(1'b1), .clk(clk), .Q(register_1_q), .clr(reset));
  // Probe on multiplexer_1_out
  // Probe on register_1_q
  POR por_1 (.out(reset));
  // Probe on dadomem
  // Probe on addr
  assign bit_extender_1_out = {{24{1'b0}}, dadomem};  // Bit_Extender bit_extender_1
  // DualRAM #(.asyncread("true"), .dataWidth(32)) dualram_1: pin names not known; wires that end beside it: register_1_q, 1'b0, 1'b1, clk, addr, MemWrite, MemRead, clk, {dualram_1_p9[31:29], moveh_l, restol1, dualram_1_p9[23:20], restol2, dualram_1_p9[15:12], RaLn3, RbLn3, dualram_1_p9[7:4], RaLn4, RbLn4}
  pc_control pc_control_1 (
    .is_zero(is_zero), .sig_brzr(Sig_BRZR), .sig_bnzr(Sig_BNZR), .sig_jr(Sig_JR), .sig_brzi(Sig_BRZI),
    .muxPC(pc_control_1_muxpc));
  Adder adder_1 (.a(8'h1), .b(register_1_q), .out(adder_1_out));  // open: cin, cout
  Adder adder_2 (.a(bit_extender_2_out), .b(register_1_q), .out(adder_2_out));  // open: cin, cout
  // Probe on pc_control_1_muxpc
  // Probe on bit_extender_2_out
  Multiplexer #(.select(2), .width(8)) multiplexer_1 (
    .in0(adder_1_out), .in1(breg_1_obln2), .in2(adder_2_out), .out(multiplexer_1_out),
    .sel(pc_control_1_muxpc));  // open: in3
  // Probe on {dualram_1_p9[31:29], moveh_l, restol1, dualram_1_p9[23:20], restol2, dualram_1_p9[15:12], RaLn3, RbLn3, dualram_1_p9[7:4], RaLn4, RbLn4}
  // Probe on breg_1_obln2
  assign bit_extender_2_out = {{4{restol2[3]}}, restol2};  // Bit_Extender bit_extender_2
  // Probe on restol2
  // Probe on restol2[1:0]
  // Probe on restol2[3:2]
  // Probe on {dualram_1_p9[31:29], moveh_l, restol1}
  // Probe on dadosmem
  Multiplexer #(.width(2)) multiplexer_2 (.in0(restol1[3:2]), .in1(2'b00), .out(multiplexer_2_out), .sel(is_move));
  Multiplexer #(.width(8)) multiplexer_3 (
    .in0(dadosmem), .in1(multiplexer_4_out), .out(multiplexer_3_out), .sel(MuxL1Src));
  is_mov is_mov_1 (.opcode({dualram_1_p9[31:29], moveh_l}), .is_move(is_move));
  Breg breg_1 (
    .DataL1(multiplexer_3_out), .DataL3(DadoL3), .DataL4(DadoL4), .RegWriteLn1(RegWriteL1), .clock(clk),
    .RegWriteLn3(RegWriteL3), .RegWriteLn4(RegWriteL4), .reset(reset), .RaLn1(multiplexer_2_out),
    .RbLn1(restol1[1:0]), .RaLn2(restol2[3:2]), .RbLn2(restol2[1:0]), .RaLn3(RaLn3), .RbLn3(RbLn3),
    .RaLn4(RaLn4), .RbLn4(RbLn4), .OALn1(dadomem), .OBLn1(addr), .OALn2(breg_1_oaln2), .OBLn2(breg_1_obln2),
    .OALn3(breg_1_oaln3), .OBLn3(breg_1_obln3), .OALn4(breg_1_oaln4), .OBLn4(breg_1_obln4));
  control control_1 (
    .InstrL1({dualram_1_p9[31:29], moveh_l}), .InstrL2(dualram_1_p9[23:20]), .InstrL3(dualram_1_p9[15:12]),
    .InstrL4(dualram_1_p9[7:4]), .MemWriteL1(MemWrite), .MemrRead(MemRead), .MuxL1Src(MuxL1Src),
    .RegWriteL1(RegWriteL1), .Sig_BRZR(Sig_BRZR), .Sig_BRZI(Sig_BRZI), .Sig_JR(Sig_JR), .Sig_BNZR(Sig_BNZR),
    .RegWriteL3(RegWriteL3), .OpULA1(control_1_opula1), .RegWriteL4(RegWriteL4), .OpULA2(control_1_opula2));
  // Probe on dadomem
  zero zero_1 (.in_1(breg_1_oaln2), .iszero(is_zero));
  move move_1 (.r0(dadomem), .imm(restol1), .movH(move_1_movh), .movL(move_1_movl));
  Multiplexer #(.width(8)) multiplexer_4 (.in0(move_1_movh), .in1(move_1_movl), .out(multiplexer_4_out), .sel(moveh_l));
  // Probe on multiplexer_4_out
  ula L3 (.entradaA(breg_1_oaln3), .entradaB(breg_1_obln3), .OpULA(control_1_opula1), .saidaULA(DadoL3));
  ula L4 (.entradaA(breg_1_oaln4), .entradaB(breg_1_obln4), .OpULA(control_1_opula2), .saidaULA(DadoL4));
  // Probe on DadoL3
  // Probe on DadoL4

  // Notes on the sheet:
  //   ULA1
  //   LD/ST/MOV
  //   ULA2
  //   BR/JMP
endmodule

module ula (
  input  [7:0] entradaA,
  input  [7:0] entradaB,
  input  [2:0] OpULA,
  output [7:0] saidaULA
);

  wire nor_1_out, or_2_out;
  wire [7:0] adder_1_out, adder_2_out, bit_extender_1_out, multiplexer_1_out, multiplexer_2_out, or_1_out,
       shifter_1_out, shifter_2_out, subtractor_1_out;

  Adder adder_1 (.a(entradaA), .b(entradaB), .out(adder_1_out));  // open: cin, cout
  Subtractor subtractor_1 (.a(entradaA), .b(entradaB), .out(subtractor_1_out));  // open: bin, bout
  assign or_1_out = entradaA | entradaB;  // OR_Gate or_1, 8 bits wide
  Shifter shifter_1 (.in(entradaA), .\dist (entradaB[2:0]), .out(shifter_1_out));
  or or_2 (or_2_out, entradaB[3], entradaB[4], entradaB[5], entradaB[6], entradaB[7]);
  Shifter #(.shift("lr")) shifter_2 (.in(entradaA), .\dist (entradaB[2:0]), .out(shifter_2_out));
  Adder adder_2 (.a(entradaA), .b(8'h1), .out(adder_2_out));  // open: cin, cout
  nor nor_1 (nor_1_out, entradaB[0], entradaB[1], entradaB[2], entradaB[3], entradaB[4], entradaB[5], entradaB[6], entradaB[7]);
  Multiplexer #(.width(8)) multiplexer_1 (
    .in0(shifter_1_out), .in1({8{1'b0}}), .out(multiplexer_1_out), .sel(or_2_out));
  Multiplexer #(.width(8)) multiplexer_2 (
    .in0({8{1'b0}}), .in1(shifter_2_out), .out(multiplexer_2_out), .sel(or_2_out));
  assign bit_extender_1_out = {{7{nor_1_out}}, nor_1_out};  // Bit_Extender bit_extender_1
  Multiplexer #(.select(3), .width(8)) multiplexer_3 (
    .in0(adder_1_out), .in1(subtractor_1_out), .in2(adder_2_out), .in3(or_1_out), .in4(bit_extender_1_out),
    .in5(multiplexer_1_out), .in6(multiplexer_2_out), .out(saidaULA), .sel(OpULA));  // open: in7
endmodule

module Breg (
  input  [7:0] DataL1,
  input  [7:0] DataL3,
  input  [7:0] DataL4,
  input  RegWriteLn1,
  input  clock,
  input  RegWriteLn3,
  input  RegWriteLn4,
  input  reset,
  input  [1:0] RaLn1,
  input  [1:0] RbLn1,
  input  [1:0] RaLn2,
  input  [1:0] RbLn2,
  input  [1:0] RaLn3,
  input  [1:0] RbLn3,
  input  [1:0] RaLn4,
  input  [1:0] RbLn4,
  output [7:0] OALn1,
  output [7:0] OBLn1,
  output [7:0] OALn2,
  output [7:0] OBLn2,
  output [7:0] OALn3,
  output [7:0] OBLn3,
  output [7:0] OALn4,
  output [7:0] OBLn4
);

  wire demultiplexer_4_out0, demultiplexer_4_out1, demultiplexer_4_out2, demultiplexer_4_out3,
       demultiplexer_5_out0, demultiplexer_5_out1, demultiplexer_5_out2, demultiplexer_5_out3,
       demultiplexer_6_out0, demultiplexer_6_out1, demultiplexer_6_out2, demultiplexer_6_out3, or_1_out,
       or_2_out, or_6_out, or_8_out;
  wire [7:0] demultiplexer_1_out0, demultiplexer_1_out1, demultiplexer_1_out2, demultiplexer_1_out3,
       demultiplexer_2_out0, demultiplexer_2_out1, demultiplexer_2_out2, demultiplexer_2_out3,
       demultiplexer_3_out0, demultiplexer_3_out1, demultiplexer_3_out2, demultiplexer_3_out3,
       multiplexer_1_out, multiplexer_2_out, multiplexer_3_out, or_3_out, or_4_out, or_5_out, or_7_out, R0_q,
       R1_q, R2_q, R3_q;

  Multiplexer #(.width(8)) multiplexer_1 (.in0({8{1'b0}}), .in1(DataL1), .out(multiplexer_1_out), .sel(RegWriteLn1));
  Demultiplexer #(.select(2), .width(8)) demultiplexer_1 (
    .out0(demultiplexer_1_out0), .out1(demultiplexer_1_out1), .out2(demultiplexer_1_out2),
    .out3(demultiplexer_1_out3), .in(multiplexer_1_out), .sel(RaLn1));
  Multiplexer #(.width(8)) multiplexer_2 (.in0({8{1'b0}}), .in1(DataL3), .out(multiplexer_2_out), .sel(RegWriteLn3));
  Demultiplexer #(.select(2), .width(8)) demultiplexer_2 (
    .out0(demultiplexer_2_out0), .out1(demultiplexer_2_out1), .out2(demultiplexer_2_out2),
    .out3(demultiplexer_2_out3), .in(multiplexer_2_out), .sel(RaLn3));
  Multiplexer #(.width(8)) multiplexer_3 (.in0({8{1'b0}}), .in1(DataL4), .out(multiplexer_3_out), .sel(RegWriteLn4));
  Demultiplexer #(.select(2), .width(8)) demultiplexer_3 (
    .out0(demultiplexer_3_out0), .out1(demultiplexer_3_out1), .out2(demultiplexer_3_out2),
    .out3(demultiplexer_3_out3), .in(multiplexer_3_out), .sel(RaLn4));
  Demultiplexer #(.select(2)) demultiplexer_4 (
    .out0(demultiplexer_4_out0), .out1(demultiplexer_4_out1), .out2(demultiplexer_4_out2),
    .out3(demultiplexer_4_out3), .in(RegWriteLn1), .sel(RaLn1));
  Demultiplexer #(.select(2)) demultiplexer_5 (
    .out0(demultiplexer_5_out0), .out1(demultiplexer_5_out1), .out2(demultiplexer_5_out2),
    .out3(demultiplexer_5_out3), .in(RegWriteLn3), .sel(RaLn3));
  Demultiplexer #(.select(2)) demultiplexer_6 (
    .out0(demultiplexer_6_out0), .out1(demultiplexer_6_out1), .out2(demultiplexer_6_out2),
    .out3(demultiplexer_6_out3), .in(RegWriteLn4), .sel(RaLn4));
  or or_1 (or_1_out, demultiplexer_4_out0, demultiplexer_5_out0, demultiplexer_6_out0);
  or or_2 (or_2_out, demultiplexer_4_out1, demultiplexer_5_out1, demultiplexer_6_out1);
  assign or_3_out = demultiplexer_1_out2 | demultiplexer_2_out2 | demultiplexer_3_out2;  // OR_Gate or_3, 8 bits wide
  assign or_4_out = demultiplexer_3_out0 | demultiplexer_2_out0 | demultiplexer_1_out0;  // OR_Gate or_4, 8 bits wide
  assign or_5_out = demultiplexer_1_out1 | demultiplexer_2_out1 | demultiplexer_3_out1;  // OR_Gate or_5, 8 bits wide
  or or_6 (or_6_out, demultiplexer_4_out2, demultiplexer_5_out2, demultiplexer_6_out2);
  assign or_7_out = demultiplexer_1_out3 | demultiplexer_2_out3 | demultiplexer_3_out3;  // OR_Gate or_7, 8 bits wide
  or or_8 (or_8_out, demultiplexer_4_out3, demultiplexer_5_out3, demultiplexer_6_out3);
  // Probe on or_4_out
  // Probe on or_1_out
  // Probe on or_3_out
  Register R0 (.D(or_4_out), .en(or_1_out), .clk(clock), .Q(R0_q), .clr(reset));
  Register R1 (.D(or_5_out), .en(or_2_out), .clk(clock), .Q(R1_q), .clr(reset));
  Register R2 (.D(or_3_out), .en(or_6_out), .clk(clock), .Q(R2_q), .clr(reset));
  Register R3 (.D(or_7_out), .en(or_8_out), .clk(clock), .Q(R3_q), .clr(reset));
  Multiplexer #(.select(2), .width(8)) multiplexer_4 (
    .in0(R0_q), .in1(R1_q), .in2(R2_q), .in3(R3_q), .out(OALn1), .sel(RaLn1));
  Multiplexer #(.select(2), .width(8)) multiplexer_5 (
    .in0(R0_q), .in1(R1_q), .in2(R2_q), .in3(R3_q), .out(OBLn1), .sel(RbLn1));
  Multiplexer #(.select(2), .width(8)) multiplexer_6 (
    .in0(R0_q), .in1(R1_q), .in2(R2_q), .in3(R3_q), .out(OALn2), .sel(RaLn2));
  Multiplexer #(.select(2), .width(8)) multiplexer_7 (
    .in0(R0_q), .in1(R1_q), .in2(R2_q), .in3(R3_q), .out(OBLn2), .sel(RbLn2));
  Multiplexer #(.select(2), .width(8)) multiplexer_8 (
    .in0(R0_q), .in1(R1_q), .in2(R2_q), .in3(R3_q), .out(OALn3), .sel(RaLn3));
  Multiplexer #(.select(2), .width(8)) multiplexer_9 (
    .in0(R0_q), .in1(R1_q), .in2(R2_q), .in3(R3_q), .out(OBLn3), .sel(RbLn3));
  Multiplexer #(.select(2), .width(8)) multiplexer_10 (
    .in0(R0_q), .in1(R1_q), .in2(R2_q), .in3(R3_q), .out(OALn4), .sel(RaLn4));
  Multiplexer #(.select(2), .width(8)) multiplexer_11 (
    .in0(R0_q), .in1(R1_q), .in2(R2_q), .in3(R3_q), .out(OBLn4), .sel(RbLn4));
endmodule

module control (
  input  [3:0] InstrL1,
  input  [3:0] InstrL2,
  input  [3:0] InstrL3,
  input  [3:0] InstrL4,
  output MemWriteL1,
  output MemrRead,
  output MuxL1Src,
  output RegWriteL1,
  output Sig_BRZR,
  output Sig_BRZI,
  output Sig_JR,
  output Sig_BNZR,
  output RegWriteL3,
  output [2:0] OpULA1,
  output RegWriteL4,
  output [2:0] OpULA2
);

  controlL1 controll1_1 (
    .Op3(InstrL1[3]), .Op2(InstrL1[2]), .Op1(InstrL1[1]), .Op0(InstrL1[0]), .MemWriteL1(MemWriteL1),
    .MemRead(MemrRead), .MuxL1Src(MuxL1Src), .RegWriteL1(RegWriteL1));
  l1 l1_1 (
    .op3(InstrL2[3]), .op2(InstrL2[2]), .op1(InstrL2[1]), .op0(InstrL2[0]), .Sig_BRZR(Sig_BRZR),
    .Sig_BRZI(Sig_BRZI), .Sig_JR(Sig_JR), .Sig_BNZR(Sig_BNZR));
  controlL3L4 controll3l4_1 (
    .ULA1(InstrL3), .ULA2(InstrL4), .RegWriteULA1(RegWriteL3), .OpULA1(OpULA1), .RegWriteULA2(RegWriteL4),
    .OpULA2(OpULA2));
endmodule

module move (
  input  [7:0] r0,
  input  [3:0] imm,
  output [7:0] movH,
  output [7:0] movL
);


  assign movH = {imm, r0[3:0]};
  assign movL = {r0[7:4], imm};
endmodule

module controlL1 (
  input  Op3,
  input  Op2,
  input  Op1,
  input  Op0,
  output MemWriteL1,
  output MemRead,
  output MuxL1Src,
  output RegWriteL1
);

  wire and_4_out, and_5_out, not_1_out, not_2_out, not_3_out;

  not not_1 (not_1_out, Op3);
  not not_2 (not_2_out, Op1);
  not not_3 (not_3_out, Op0);
  and and_1 (MemWriteL1, not_1_out, Op2, not_2_out, Op0);
  and and_2 (MemRead, not_1_out, Op2, not_2_out, not_3_out);
  and and_3 (MuxL1Src, not_1_out, Op2, Op1);
  and and_4 (and_4_out, not_1_out, Op2, not_3_out);
  and and_5 (and_5_out, not_1_out, Op2, Op1);
  or or_1 (RegWriteL1, and_4_out, and_5_out);
endmodule

module controlL2 (
  input  Op3,
  input  Op2,
  input  Op1,
  input  Op0,
  output Sig_BRZR,
  output Sig_BRZI,
  output Sig_JR,
  output Sig_BNZR
);

  wire not_1_out, not_2_out, not_3_out, not_4_out;

  not not_1 (not_1_out, Op3);
  not not_2 (not_2_out, Op2);
  not not_3 (not_3_out, Op1);
  not not_4 (not_4_out, Op0);
  and and_1 (Sig_BRZR, not_1_out, not_2_out, not_3_out, not_4_out);
  and and_2 (Sig_BRZI, not_1_out, not_2_out, not_3_out, Op0);
  and and_3 (Sig_JR, not_1_out, not_2_out, Op1, not_4_out);
  and and_4 (Sig_BNZR, not_1_out, not_2_out, Op1, Op0);
endmodule

module controlL3L4 (
  input  [3:0] ULA1,
  input  [3:0] ULA2,
  output RegWriteULA1,
  output [2:0] OpULA1,
  output RegWriteULA2,
  output [2:0] OpULA2
);

  wire nand_1_out, nand_2_out;

  nand nand_1 (nand_1_out, ULA1[0], ULA1[1], ULA1[2]);
  nand nand_2 (nand_2_out, ULA2[0], ULA2[1], ULA2[2]);
  and and_1 (RegWriteULA1, nand_1_out, ULA1[3]);
  and and_2 (RegWriteULA2, nand_2_out, ULA2[3]);
  Multiplexer #(.width(3)) multiplexer_1 (.in0(3'b000), .in1(ULA2[2:0]), .out(OpULA2), .sel(RegWriteULA2));
  Multiplexer #(.width(3)) multiplexer_2 (.in0(3'b000), .in1(ULA1[2:0]), .out(OpULA1), .sel(RegWriteULA1));
endmodule

module zero (
  input  [7:0] in_1,
  output iszero
);

  nor nor_1 (iszero, in_1[0], in_1[1], in_1[2], in_1[3], in_1[4], in_1[5], in_1[6], in_1[7]);
endmodule

module pc_control (
  input  is_zero,
  input  sig_brzr,
  input  sig_bnzr,
  input  sig_jr,
  input  sig_brzi,
  output [1:0] muxPC
);

  wire and_1_out, and_3_out, not_1_out;

  not not_1 (not_1_out, is_zero);
  and and_1 (and_1_out, sig_bnzr, not_1_out);
  and and_2 (muxPC[1], is_zero, sig_brzi);
  and and_3 (and_3_out, is_zero, sig_brzr);
  or or_1 (muxPC[0], and_3_out, and_1_out, sig_jr);
endmodule

module is_mov (
  input  [3:0] opcode,
  output is_move
);

  wire not_1_out;

  not not_1 (not_1_out, opcode[3]);
  and and_1 (is_move, opcode[1], opcode[2], not_1_out);
endmodule

module l1 (
  input  op3,
  input  op2,
  input  op1,
  input  op0,
  output Sig_BRZR,
  output Sig_BRZI,
  output Sig_JR,
  output Sig_BNZR
);

  wire not_1_out, not_2_out, not_3_out, not_4_out;

  not not_1 (not_1_out, op3);
  not not_2 (not_2_out, op2);
  not not_3 (not_3_out, op1);
  not not_4 (not_4_out, op0);
  and and_1 (Sig_BRZR, not_1_out, not_2_out, not_3_out, not_4_out);
  and and_2 (Sig_BRZI, not_1_out, not_2_out, not_3_out, op0);
  and and_3 (Sig_JR, not_1_out, not_2_out, op1, not_4_out);
  and and_4 (Sig_BNZR, not_1_out, not_2_out, op1, op0);
endmodule
